// Logisim project muxrisccore.circ as structural Verilog: 1 circuit, main circuit main
module main (
);

  wire clock_1_out, clock_2_out, clock_3_out, clock_4_out, comparator_1_eq, comparator_2_eq, counter_1_q,
       multiplexer_2_out, multiplexer_4_out, or_1_out;
  wire [1:0] bitselector_1_out, register_1_q;
  wire [15:0] bitselector_2_out, counter_2_q, multiplexer_3_out;
  wire [63:0] multiplexer_1_out, multiplexer_5_out, ram_1_dout;

  Multiplexer #(.width(64)) multiplexer_1 (
    .in0(ram_1_dout), .in1({64{1'b0}}), .out(multiplexer_1_out), .sel(multiplexer_2_out));
  Multiplexer #(.select(2)) multiplexer_2 (
    .in0(1'b0), .in1(counter_1_q), .out(multiplexer_2_out), .sel(register_1_q));  // open: in2, in3
  Register #(.trigger("falling"), .width(2)) register_1 (
    .D(bitselector_1_out), .en(1'b1), .clk(clock_1_out), .Q(register_1_q));  // open: clr
  BitSelector #(.group(2), .width(64)) bitselector_1 (.in(multiplexer_1_out), .out(bitselector_1_out), .sel({5{1'b0}}));
  Clock clock_1 (.out(clock_1_out));
  Comparator #(.width(2)) comparator_1 (.a(register_1_q), .b(2'b00), .eq(comparator_1_eq));  // open: gt, lt
  or or_1 (or_1_out, comparator_1_eq, comparator_2_eq);
  Comparator #(.width(2)) comparator_2 (.a(register_1_q), .b(2'b01), .eq(comparator_2_eq));  // open: gt, lt
  Clock clock_2 (.out(clock_2_out));
  Counter #(.max('h1), .width(1)) counter_1 (
    .count(comparator_2_eq), .Q(counter_1_q), .clk(clock_2_out), .clr(comparator_1_eq));  // open: load, D, carry, up
  BitSelector #(.group(16), .width(64)) bitselector_2 (.in(ram_1_dout), .out(bitselector_2_out), .sel(2'b00));
  Clock clock_3 (.out(clock_3_out));
  Counter #(.max('hffff), .trigger("falling"), .width(16)) counter_2 (
    .load(counter_1_q), .D(bitselector_2_out), .count(or_1_out), .Q(counter_2_q), .clk(clock_3_out));  // open: carry, up, clr
  Multiplexer #(.select(2), .width(16)) multiplexer_3 (
    .in0(counter_2_q), .in1(counter_2_q), .out(multiplexer_3_out), .sel(register_1_q));  // open: in2, in3
  Multiplexer #(.select(2)) multiplexer_4 (
    .in0(1'b0), .in1(1'b0), .out(multiplexer_4_out), .sel(register_1_q));  // open: in2, in3
  RAM #(.addrWidth(16), .dataWidth(64), .enables("line"), .\type ("nonvolatile")) ram_1 (
    .addr(multiplexer_3_out), .we(multiplexer_4_out), .clk(clock_4_out), .din(multiplexer_5_out),
    .dout(ram_1_dout));
  Clock clock_4 (.out(clock_4_out));
  Multiplexer #(.select(2), .width(64)) multiplexer_5 (
    .in0({64{1'b0}}), .in1({64{1'b0}}), .out(multiplexer_5_out), .sel(register_1_q));  // open: in2, in3
endmodule
